// Logisim project alu.circ as structural Verilog: 4 circuits, main circuit AND_2bit
module alu (
  input  [31:0] A,
  input  [31:0] B,
  input  [3:0] ALUSel,
  output [31:0] Result
);

  wire [31:0] add0, and1;

  Adder #(.width(32)) adder_1 (.a(A), .b(B), .out(add0));  // open: cin, cout
  AND_32bit and_32bit_1 (.in_1(A), .in_2(B), .out_3(and1));

  // Notes on the sheet:
  //   INPUTS to your circuit
  //   DON'T CHANGE THE LOCATIONS OF THE INPUTS AND OUTPUTS!
  //   OUTPUT from your circuit
endmodule

module AND_2bit (
  input  [1:0] in_1,
  input  [1:0] in_2,
  output [1:0] out_3
);

  and and_1 (out_3[0], in_1[0], in_2[0]);
  and and_2 (out_3[1], in_1[1], in_2[1]);
endmodule

module AND_8bit (
  input  [7:0] in_1,
  input  [7:0] in_2,
  output [7:0] out_3
);

  AND_2bit and_2bit_1 (.in_1(in_1[1:0]), .in_2(in_2[1:0]), .out_3(out_3[1:0]));
  AND_2bit and_2bit_2 (.in_1(in_1[3:2]), .in_2(in_2[3:2]), .out_3(out_3[3:2]));
  AND_2bit and_2bit_3 (.in_1(in_1[5:4]), .in_2(in_2[5:4]), .out_3(out_3[5:4]));
  AND_2bit and_2bit_4 (.in_1(in_1[7:6]), .in_2(in_2[7:6]), .out_3(out_3[7:6]));
endmodule

module AND_32bit (
  input  [31:0] in_1,
  input  [31:0] in_2,
  output [31:0] out_3
);

  AND_8bit and_8bit_1 (.in_1(in_1[7:0]), .in_2(in_2[7:0]), .out_3(out_3[7:0]));
  AND_8bit and_8bit_2 (.in_1(in_1[15:8]), .in_2(in_2[15:8]), .out_3(out_3[15:8]));
  AND_8bit and_8bit_3 (.in_1(in_1[23:16]), .in_2(in_2[23:16]), .out_3(out_3[23:16]));
  AND_8bit and_8bit_4 (.in_1(in_1[31:24]), .in_2(in_2[31:24]), .out_3(out_3[31:24]));
endmodule
